# Fritzing sketch ColorMsg (saved by Fritzing 0.9.2b)
breadboards: 1

parts:
  Arduino1 = Arduino Uno (Rev3)
  LCD2 = LCD screen
  R2 = Trimmer Potentiometer [maximum_resistance=10kΩ package=THT]
  LED1 = LED - 5mm [color="Blue (430nm)" package="5 mm [THT]"]
  LED2 = LED - 5mm [color="Red (633nm)" package="5 mm [THT]"]
  LED3 = LED - 5mm [color="Green (565nm)" package="5 mm [THT]"]
  R3 = Resistor [tolerance=±5% resistance=100 package=THT]
  R4 = Resistor [tolerance=±5% resistance=100 package=THT]
  R5 = Resistor [tolerance=±5% resistance=100 package=THT]
  J1 = Piezo Speaker
  R6 = Resistor [tolerance=±5% resistance=220 package=THT]

nets:
  N1: Arduino1.D8, R4.Pin_0
  N2: Arduino1.D9_PWM, R3.Pin_0
  N3: Arduino1.D10_PWM/SS, J1.pin2
  N4: Arduino1.D11_PWM/MOSI, LCD2.E
  N5: Arduino1.D12/MISO, LCD2.RS
  GND: Arduino1.GND, LCD2.VSS, LCD2.R/W, LCD2.LED-, LED1.anode, LED2.anode, LED3.anode, R6.Pin_1
  N6: Arduino1.D2, LCD2.DB7
  N7: Arduino1.D3_PWM, LCD2.DB6
  N8: Arduino1.D4, LCD2.DB5
  N9: Arduino1.D5_PWM, LCD2.DB4
  N10: Arduino1.D7, R5.Pin_0
  N11: Arduino1.3V3, LCD2.LED+
  5V: Arduino1.5V, LCD2.VDD
  N12: LCD2.V0, R2.wiper
  N13: LED1.cathode, R5.Pin_1
  N14: LED2.cathode, R3.Pin_1
  N15: LED3.cathode, R4.Pin_1
  N16: J1.pin1, R6.Pin_0

notes:
  http://ArduinoColorMsg.codeplex.com
